// Logisim project LEDtest.circ as structural Verilog: 1 circuit, main circuit main
module main (
  input  [15:0] in_1,
  input  [15:0] in_2,
  input  [15:0] in_3,
  input  [15:0] in_4,
  input  [15:0] in_5,
  input  [15:0] in_6,
  input  [15:0] in_7,
  input  [15:0] in_8,
  input  [15:0] in_9,
  input  [15:0] in_10,
  input  [15:0] in_11,
  input  [15:0] in_12,
  input  [15:0] in_13,
  input  [15:0] in_14,
  input  [15:0] in_15
);

  DotMatrix #(.matrixcols(8), .matrixrows(16)) dotmatrix_1 (
    .col0(in_8), .col1(in_9), .col2(in_10), .col3(in_11), .col4(in_12), .col5(in_13), .col6(in_14),
    .col7(in_15));
  DotMatrix #(.matrixrows(16)) dotmatrix_2 ();  // open: col0, col1, col2, col3, col4
  DotMatrix #(.matrixrows(16)) dotmatrix_3 ();  // open: col0, col1, col2, col3, col4
  DotMatrix #(.matrixrows(16)) dotmatrix_4 ();  // open: col0, col1, col2, col3, col4
  DotMatrix #(.matrixrows(16)) dotmatrix_5 ();  // open: col0, col1, col2, col3, col4
  DotMatrix #(.matrixrows(16)) dotmatrix_6 ();  // open: col0, col1, col2, col3, col4
  DotMatrix #(.matrixrows(16)) dotmatrix_7 ();  // open: col0, col1, col2, col3, col4
endmodule
