// Logisim project microcpu.circ as structural Verilog: 7 circuits, main circuit main
// address
module main (
  input  reset
);

  wire c, clock_1_out, clock_2_out, datawrite, dwrite, imload, irload, n, not_1_out, pcload, swrite, z;
  wire [1:0] addrsel, datasel, op2sel, pcsel, regsrc;
  wire [2:0] irlogic_1_dregsel, irlogic_1_sregsel, irlogic_1_tregsel;
  wire [3:0] aluop;
  wire [6:0] opcode;
  wire [7:0] ucodelogic_1_ucounter;
  wire [15:0] aluout, dreg, immed, multiplexer_1_out, multiplexer_2_out, multiplexer_3_out,
       multiplexer_4_out, pc, r0, r1, r2, r3, r4, ram_1_data, registerfile_1_r5, registerfile_1_r6,
       registerfile_1_r7, sreg, treg;

  // Probe on c
  // Probe on z
  // Probe on n
  // Probe on opcode
  Clock clock_1 (.out(clock_1_out));
  // Probe on ucodelogic_1_ucounter
  ucodelogic ucodelogic_1 (
    .n(n), .z(z), .opcode(opcode), .aluop(aluop), .op2sel(op2sel), .datawrite(datawrite), .addrsel(addrsel),
    .pcsel(pcsel), .pcload(pcload), .dwrite(dwrite), .irload(irload), .imload(imload), .regsrc(regsrc),
    .ucounter(ucodelogic_1_ucounter), .datasel(datasel), .swrite(swrite), .c(c));
  // Probe on multiplexer_1_out
  RAM #(.addrWidth(16), .dataWidth(16)) ram_1 (
    .addr(multiplexer_1_out), .data(ram_1_data), .clk(clock_1_out), .ld(not_1_out), .clr(reset));  // open: sel
  not not_1 (not_1_out, datawrite);
  // Probe on aluop
  // Probe on op2sel
  // Probe on datawrite
  // Probe on addrsel
  // Probe on pcsel
  // Probe on pcload
  // Probe on dwrite
  // Probe on irload
  // Probe on imload
  // Probe on regsrc
  // Probe on datasel
  // Probe on swrite
  Multiplexer #(.select(2), .width(16), .enable("false")) multiplexer_1 (
    .in0(pc), .in1(immed), .in2(aluout), .in3(sreg), .out(multiplexer_1_out), .sel(addrsel));
  // Probe on ram_1_data
  assign ram_1_data = datawrite ? multiplexer_2_out : 16'bz;  // Controlled_Buffer controlled_buffer_1
  Multiplexer #(.select(2), .width(16), .enable("false")) multiplexer_2 (
    .in0(pc), .in1(dreg), .in2(treg), .in3(aluout), .out(multiplexer_2_out), .sel(datasel));
  // Probe on pc
  Register #(.width(16)) register_1 (.D(ram_1_data), .en(imload), .Q(immed), .clk(clock_2_out), .clr(reset));
  Clock clock_2 (.out(clock_2_out));
  pclogic pclogic_1 (.imreg(immed), .sreg(sreg), .pcout(pc), .pcsel(pcsel), .pcload(pcload), .reset(reset));
  Multiplexer #(.select(2), .width(16), .enable("false")) multiplexer_3 (
    .in0(ram_1_data), .in1(immed), .in2(aluout), .in3(sreg), .out(multiplexer_3_out), .sel(regsrc));
  irlogic irlogic_1 (
    .instruction(ram_1_data), .irload(irload), .dregsel(irlogic_1_dregsel), .sregsel(irlogic_1_sregsel),
    .tregsel(irlogic_1_tregsel), .opcode(opcode));  // open: reset
  registerfile registerfile_1 (
    .dwrite(dwrite), .regval(multiplexer_3_out), .sreg(sreg), .treg(treg), .dsel(irlogic_1_dregsel),
    .ssel(irlogic_1_sregsel), .tsel(irlogic_1_tregsel), .r0(r0), .r1(r1), .r2(r2), .r7(registerfile_1_r7),
    .r6(registerfile_1_r6), .r5(registerfile_1_r5), .r4(r4), .r3(r3), .dreg(dreg), .swrite(swrite),
    .reset(reset));  // open: twrite
  // Probe on r0
  // Probe on r1
  // Probe on r2
  // Probe on r3
  // Probe on r4
  // Probe on registerfile_1_r5
  // Probe on registerfile_1_r6
  // Probe on registerfile_1_r7
  // Probe on irlogic_1_dregsel
  // Probe on irlogic_1_sregsel
  // Probe on irlogic_1_tregsel
  // Probe on opcode
  Multiplexer #(.select(2), .width(16), .enable("false")) multiplexer_4 (
    .in0(treg), .in1(immed), .in2({16{1'b0}}), .in3(16'h1), .out(multiplexer_4_out), .sel(op2sel));
  ALU alu_1 (.Zero(z), .Negative(n), .Result(aluout), .aluop(aluop), .A(sreg), .B(multiplexer_4_out), .Carry(c));
  // Probe on aluop
  // Probe on aluout
  DotMatrix #(.matrixrows(16)) dotmatrix_1 (.col0(r0), .col1(r1), .col2(r2), .col3(r3), .col4(r4));

  // Notes on the sheet:
  //   RAM
  //   Microcode Logic
  //   Microcoded 16-bit CPU
  //   Immed
  //   PC
  //   IR
  //   Regs
  //   ALU
  //   SNAKE
endmodule

module irlogic (
  input  [15:0] instruction,
  input  irload,
  input  reset,
  output [2:0] dregsel,
  output [2:0] sregsel,
  output [2:0] tregsel,
  output [6:0] opcode
);

  wire clock_1_out;

  Clock clock_1 (.out(clock_1_out));
  Register #(.width(16)) IR (
    .D(instruction), .en(irload), .Q({opcode, tregsel, sregsel, dregsel}), .clk(clock_1_out), .clr(reset));

  // Notes on the sheet:
  //   IR Logic
endmodule

module registerfile (
  input  [15:0] regval,
  input  reset,
  input  dwrite,
  input  swrite,
  input  twrite,
  input  [2:0] dsel,
  input  [2:0] ssel,
  input  [2:0] tsel,
  output [15:0] r0,
  output [15:0] r1,
  output [15:0] r2,
  output [15:0] r3,
  output [15:0] r4,
  output [15:0] r5,
  output [15:0] r6,
  output [15:0] r7,
  output [15:0] dreg,
  output [15:0] sreg,
  output [15:0] treg
);

  wire clock_1_out, demultiplexer_1_out0, demultiplexer_1_out1, demultiplexer_1_out2, demultiplexer_1_out3,
       demultiplexer_1_out4, demultiplexer_1_out5, demultiplexer_1_out6, demultiplexer_1_out7;

  Demultiplexer #(.select(3), .enable("false")) demultiplexer_1 (
    .out0(demultiplexer_1_out0), .out1(demultiplexer_1_out1), .out2(demultiplexer_1_out2),
    .out3(demultiplexer_1_out3), .out4(demultiplexer_1_out4), .out5(demultiplexer_1_out5),
    .out6(demultiplexer_1_out6), .out7(demultiplexer_1_out7), .in(dwrite), .sel(dsel));
  Demultiplexer #(.select(3), .enable("false")) demultiplexer_2 (
    .out0(demultiplexer_1_out0), .out1(demultiplexer_1_out1), .out2(demultiplexer_1_out2),
    .out3(demultiplexer_1_out3), .out4(demultiplexer_1_out4), .out5(demultiplexer_1_out5),
    .out6(demultiplexer_1_out6), .out7(demultiplexer_1_out7), .in(swrite), .sel(ssel));
  Demultiplexer #(.select(3), .enable("false")) demultiplexer_3 (
    .out0(demultiplexer_1_out0), .out1(demultiplexer_1_out1), .out2(demultiplexer_1_out2),
    .out3(demultiplexer_1_out3), .out4(demultiplexer_1_out4), .out5(demultiplexer_1_out5),
    .out6(demultiplexer_1_out6), .out7(demultiplexer_1_out7), .in(twrite), .sel(tsel));
  Register #(.width(16)) register_1 (.D(regval), .en(demultiplexer_1_out0), .Q(r0), .clk(clock_1_out), .clr(reset));
  Register #(.width(16)) register_2 (.D(regval), .en(demultiplexer_1_out1), .Q(r1), .clk(clock_1_out), .clr(reset));
  Register #(.width(16)) register_3 (.D(regval), .en(demultiplexer_1_out2), .Q(r2), .clk(clock_1_out), .clr(reset));
  Register #(.width(16)) register_4 (.D(regval), .en(demultiplexer_1_out3), .Q(r3), .clk(clock_1_out), .clr(reset));
  Register #(.width(16)) register_5 (.D(regval), .en(demultiplexer_1_out4), .Q(r4), .clk(clock_1_out), .clr(reset));
  Register #(.width(16)) register_6 (.D(regval), .en(demultiplexer_1_out5), .Q(r5), .clk(clock_1_out), .clr(reset));
  Register #(.width(16)) register_7 (.D(regval), .en(demultiplexer_1_out6), .Q(r6), .clk(clock_1_out), .clr(reset));
  Register #(.width(16)) register_8 (.D(regval), .en(demultiplexer_1_out7), .Q(r7), .clk(clock_1_out), .clr(reset));
  Clock clock_1 (.out(clock_1_out));
  Multiplexer #(.select(3), .width(16), .enable("false")) multiplexer_1 (
    .in0(r0), .in1(r1), .in2(r2), .in3(r3), .in4(r4), .in5(r5), .in6(r6), .in7(r7), .out(dreg), .sel(dsel));
  Multiplexer #(.select(3), .width(16), .enable("false")) multiplexer_2 (
    .in0(r0), .in1(r1), .in2(r2), .in3(r3), .in4(r4), .in5(r5), .in6(r6), .in7(r7), .out(sreg), .sel(ssel));
  Multiplexer #(.select(3), .width(16), .enable("false")) multiplexer_3 (
    .in0(r0), .in1(r1), .in2(r2), .in3(r3), .in4(r4), .in5(r5), .in6(r6), .in7(r7), .out(treg), .sel(tsel));

  // Notes on the sheet:
  //   Register File
endmodule

module ALU (
  input  [15:0] A,
  input  [15:0] B,
  input  [3:0] aluop,
  output Carry,
  output Zero,
  output Negative,
  output [15:0] Result
);

  wire adder_1_cout, or_2_out, subtractor_1_bout;
  wire [15:0] adder_1_out, and_1_out, divider_1_out, divider_1_rem, multiplier_1_out, nand_1_out, nor_1_out,
       not_1_out, or_1_out, shifter_1_out, shifter_2_out, shifter_3_out, shifter_4_out, shifter_5_out,
       subtractor_1_out, xor_1_out;

  Adder #(.width(16)) adder_1 (.a(A), .b(B), .out(adder_1_out), .cin(1'b0), .cout(adder_1_cout));
  Subtractor #(.width(16)) subtractor_1 (.a(A), .b(B), .out(subtractor_1_out), .bin(1'b0), .bout(subtractor_1_bout));
  Multiplier #(.width(16)) multiplier_1 (.a(A), .b(B), .out(multiplier_1_out), .cin({16{1'b0}}));  // open: cout
  Divider #(.width(16)) divider_1 (.a(A), .b(B), .out(divider_1_out), .upper({16{1'b0}}), .rem(divider_1_rem));
  assign and_1_out = A & B;  // AND_Gate and_1, 16 bits wide
  assign or_1_out = A | B;  // OR_Gate or_1, 16 bits wide
  assign xor_1_out = A ^ B;  // XOR_Gate xor_1, 16 bits wide
  assign nand_1_out = ~(A & B);  // NAND_Gate nand_1, 16 bits wide
  assign nor_1_out = ~(A | B);  // NOR_Gate nor_1, 16 bits wide
  assign not_1_out = ~A;  // NOT_Gate not_1, 16 bits wide
  Shifter #(.width(16)) shifter_1 (.in(A), .\dist (B[3:0]), .out(shifter_1_out));
  Shifter #(.width(16), .shift("lr")) shifter_2 (.in(A), .\dist (B[3:0]), .out(shifter_2_out));
  Shifter #(.width(16), .shift("ar")) shifter_3 (.in(A), .\dist (B[3:0]), .out(shifter_3_out));
  Shifter #(.width(16), .shift("rl")) shifter_4 (.in(A), .\dist (B[3:0]), .out(shifter_4_out));
  Shifter #(.width(16), .shift("rr")) shifter_5 (.in(A), .\dist (B[3:0]), .out(shifter_5_out));
  Multiplexer #(.select(4), .width(16), .enable("false")) multiplexer_1 (
    .in0(adder_1_out), .in1(subtractor_1_out), .in2(multiplier_1_out), .in3(divider_1_out),
    .in4(divider_1_rem), .in5(and_1_out), .in6(or_1_out), .in7(xor_1_out), .in8(nand_1_out), .in9(nor_1_out),
    .in10(not_1_out), .in11(shifter_1_out), .in12(shifter_2_out), .in13(shifter_3_out), .in14(shifter_4_out),
    .in15(shifter_5_out), .out({Negative, Result[14:0]}), .sel(aluop));
  Multiplexer #(.select(4), .enable("false")) multiplexer_2 (
    .in0(adder_1_cout), .in1(subtractor_1_bout), .in2(1'b0), .in3(1'b0), .in4(1'b0), .in5(1'b0), .in6(1'b0),
    .in7(1'b0), .in8(1'b0), .in9(1'b0), .in10(1'b0), .in11(1'b0), .in12(1'b0), .in13(1'b0), .in14(1'b0),
    .in15(1'b0), .out(Carry), .sel(aluop));
  or or_2 (or_2_out, Result[0], Result[1], Result[2], Result[3], Result[4], Result[5], Result[6], Result[7], Result[9], Result[10], Result[11], Result[12], Result[13], Result[14], Negative, Result[8]);
  not not_2 (Zero, or_2_out);

  assign Result[15] = Negative;

  // Notes on the sheet:
  //   16-bit ALU
endmodule

module pclogic (
  input  [15:0] imreg,
  input  pcload,
  input  reset,
  input  [15:0] sreg,
  input  [1:0] pcsel,
  output [15:0] pcout
);

  wire clock_1_out;
  wire [15:0] adder_1_out, adder_2_out, multiplexer_1_out;

  Adder #(.width(16)) adder_1 (.a(pcout), .b(16'h1), .out(adder_1_out));  // open: cin, cout
  Adder #(.width(16)) adder_2 (.a(pcout), .b(imreg), .out(adder_2_out));  // open: cin, cout
  Multiplexer #(.select(2), .width(16), .enable("false")) multiplexer_1 (
    .in0(adder_1_out), .in1(imreg), .in2(adder_2_out), .in3(sreg), .out(multiplexer_1_out), .sel(pcsel));
  Register #(.width(16)) PC (.D(multiplexer_1_out), .en(pcload), .Q(pcout), .clk(clock_1_out), .clr(reset));
  Clock clock_1 (.out(clock_1_out));

  // Notes on the sheet:
  //   PC Logic
endmodule

module ucodelogic (
  input  z,
  input  n,
  input  c,
  input  [6:0] opcode,
  output [3:0] aluop,
  output [1:0] op2sel,
  output datawrite,
  output [7:0] ucounter,
  output [1:0] addrsel,
  output [1:0] pcsel,
  output pcload,
  output dwrite,
  output irload,
  output imload,
  output [1:0] regsrc,
  output [1:0] datasel,
  output swrite
);

  wire clock_1_out, indexsel, multiplexer_2_out, or_1_out;
  wire [1:0] cond;
  wire [7:0] adder_1_out, multiplexer_1_out, multiplexer_3_out;
  wire [15:0] rom_2_data;
  wire [31:23] rom_1_data;

  Register Microcounter (.D(adder_1_out), .Q(ucounter), .clk(clock_1_out));  // open: en, clr
  Clock clock_1 (.out(clock_1_out));
  ROM #(.dataWidth(32)) rom_1 (
    .addr(ucounter),
    .data({rom_1_data, swrite, datasel, indexsel, cond, regsrc, imload, irload, dwrite, pcload, pcsel, addrsel, datawrite, op2sel, aluop}));  // open: sel
  ROM #(.dataWidth(16)) rom_2 (.addr(ucounter), .data(rom_2_data));  // open: sel
  or or_1 (or_1_out, z, n);
  Multiplexer #(.width(8), .enable("false")) multiplexer_1 (
    .in0(rom_2_data[7:0]), .in1(rom_2_data[15:8]), .out(multiplexer_1_out), .sel(multiplexer_2_out));
  Multiplexer #(.select(2), .enable("false")) multiplexer_2 (
    .in0(z), .in1(or_1_out), .in2(n), .in3(c), .out(multiplexer_2_out), .sel(cond));
  Multiplexer #(.width(8), .enable("false")) multiplexer_3 (
    .in0({8{1'b0}}), .in1({1'b0, opcode}), .out(multiplexer_3_out), .sel(indexsel));
  Adder adder_1 (.a(multiplexer_1_out), .b(multiplexer_3_out), .out(adder_1_out));  // open: cin, cout

  // Notes on the sheet:
  //   Control ROM
  //   contents of rom_1 (hex, n*v repeats v):
  //   2000 80800 11000 11001 11002 11003 11004 11005 11006 11007 11008 11009 1100a 1100b 1100c 1100d 26*0
  //   4000 6*0 4000 15*0 1000 1000 4000 62*0 21 20 800 800 1000c0 800 800 a00
  //   Decision ROM
  //   contents of rom_2 (hex, n*v repeats v):
  //   101 202 40*0 8282 6*0 8383 15*0 8484 8585 8686 62*0 8889 8889 0 0 8787
endmodule

module \output  (
);

  wire [15:0] r0;

  DotMatrix #(.matrixrows(16)) dotmatrix_1 (.col0(r0));  // open: col1, col2, col3, col4
endmodule
